// Digital circuit ula.dig as structural Verilog
module ula (
  input  [31:0] A,
  input  [31:0] B,
  input  [2:0] c_ula,
  output [31:0] Output,
  output zero
);

  wire Comparador_eq, Comparador_lt;
  wire [31:0] and_1_out, bitextender_1_out, bitextender_2_out, bitextender_3_out, or_1_out, Shift_Left_out,
       Sub_s, Sum_s, xor_1_out;

  Add #(.Bits(32)) Sum (.a(A), .b(B), .c_i(1'b0), .s(Sum_s));  // open: c_o
  Sub #(.Bits(32)) Sub (.a(A), .b(B), .c_i(1'b0), .s(Sub_s));  // open: c_o
  assign and_1_out = A & B;  // And and_1, 32 bits wide
  assign xor_1_out = A ^ B;  // XOr xor_1, 32 bits wide
  assign or_1_out = A | B;  // Or or_1, 32 bits wide
  BarrelShifter #(.Bits(32), .barrelSigned("true")) Shift_Left (.in(A), .shift(B[6:0]), .out(Shift_Left_out));
  Comparator #(.Signed("true"), .Bits(32)) Comparador (
    .a(A), .b(B), .eq(Comparador_eq), .lt(Comparador_lt));  // open: gt
  BitExtender #(.inputBits(1), .outputBits(32)) bitextender_1 (.in(Comparador_eq), .out(bitextender_1_out));
  BitExtender #(.inputBits(1), .outputBits(32)) bitextender_2 (.in(Comparador_lt), .out(bitextender_2_out));
  Multiplexer #(.Selector_Bits(3), .Bits(32)) multiplexer_1 (
    .sel(c_ula), .in_0(Sum_s), .in_1(Sub_s), .in_2(and_1_out), .in_3(xor_1_out), .in_4(or_1_out),
    .in_5(Shift_Left_out), .in_6(bitextender_1_out), .in_7(bitextender_2_out), .out(Output));
  BitExtender #(.inputBits(1), .outputBits(32)) bitextender_3 (.in(1'b0), .out(bitextender_3_out));
  Comparator #(.Bits(32)) comparator_1 (.a(bitextender_3_out), .b(Output), .eq(zero));  // open: gt, lt
endmodule
